// Logisim project HalfAdderLib.circ as structural Verilog: 2 circuits, main circuit HaflAdderUI
module HaflAdderUI (
);

  wire ab_p1, ab_p2, halfadder_1_carry, halfadder_1_sum;

  // DipSwitch #(.number(2)) ab: pin names not known; wires that end beside it: ab_p1, ab_p2
  HalfAdder halfadder_1 (.a(ab_p1), .b(ab_p2), .sum(halfadder_1_sum), .carry(halfadder_1_carry));
  LED sum (.in(halfadder_1_sum));
  LED carry (.in(halfadder_1_carry));
endmodule

module HalfAdder (
  input  a,
  input  b,
  output sum,
  output carry
);

  xor xor_1 (sum, a, b);
  and and_1 (carry, a, b);
endmodule
